# Fritzing sketch A019_servo_fotorresistencia_girasol (saved by Fritzing 0.8.3b)
breadboards: 1

parts:
  Parte1 = Arduino Uno (Rev3)
  J1 = Basic Servo
  R1 = Photocell (LDR) [package=THT]
  R2 = Resistor [tolerance=±5% resistance=220 package=THT]

nets:
  N1: Parte1.A0, R1.pin_0, R2.Pin_1
  5V: Parte1.5V, J1.vcc, R1.pin_1
  GND: Parte1.GND, J1.gnd, R2.Pin_0
  N2: Parte1.D8, J1.pulse
