# Fritzing sketch A026_pinmode_pullup (saved by Fritzing 0.8.3b)

parts:
  Parte1 = Arduino Uno (Rev3)
  LED1 = LED - 5mm [color="Red (633nm)" package="5 mm [THT]"]
  S3 = Pushbutton [package="[THT]"]

nets:
  N1: Parte1.GND, S3.Pin_1, S3.Pin_2
  N2: Parte1.D13/SCK, S3.Pin_4
  N3: Parte1.D5_PWM, LED1.cathode
