# Fritzing sketch A027_aref_analogread (saved by Fritzing 0.8.3b)
breadboards: 1

parts:
  Parte1 = Arduino Uno (Rev3)
  R1 = Resistor [tolerance=±5% resistance=220 package=THT]
  R2 = Resistor [tolerance=±5% resistance=220 package=THT]
  VCC1 = Battery

nets:
  N1: Parte1.A2, VCC1.+
  N2: Parte1.GND, R1.Pin_0, VCC1.-
  N3: Parte1.AREF, R1.Pin_1, R2.Pin_0
